# Fritzing sketch principal para secundarios (saved by Fritzing 0.9.4)

parts:
  Componente1 = Arduino Mega 2560 (Rev3)
  Componente2 = Arduino Nano (Rev3.0)
  Componente3 = Arduino Nano (Rev3.0)

nets:
  N1: Componente1.D18/TX1, Componente2.D2, Componente3.D2
  5V: Componente1.5V, Componente2.5V, Componente3.5V
  GND: Componente1.GND, Componente2.GND, Componente3.GND

notes:
  RX - pin 2
  Software Serial
  NÃO LIGAR DOIS USB AO MESMO TEMPO
